# Fritzing sketch climateController (saved by Fritzing 0.9.3b)
perfboards: 1

parts:
  Bauteil1 = Arduino Nano (Rev3.0)  # not connected
  J7 = female pin header, 15 pins [form="♀ (female)"]
  J6 = female pin header, 15 pins [form="♀ (female)"]
  Temperature_Sensors = female pin header, 4 pins [form="♀ (female)"]
  R2 = Resistor [tolerance=±5% resistance=1k package=THT]
  R1 = Temperature Sensor (Thermistor) [thermistor_type=NTC package=THT]
  MicroSD_Card_Pins = female pin header, 6 pins [form="♀ (female)"]
  RTClock_Pins = female pin header, 6 pins [form="♀ (female)"]
  Relay = female pin header, 4 pins [form="♀ (female)"]

nets:
  N1: J7.pin2, Temperature_Sensors.pin4, R2.Pin_0, MicroSD_Card_Pins.pin6, RTClock_Pins.pin6, Relay.pin4
  N2: J7.pin4, Temperature_Sensors.pin1, R1.pin_1, MicroSD_Card_Pins.pin5, RTClock_Pins.pin5, Relay.pin1
  N3: J7.pin5, R2.Pin_1, R1.pin_0
  N4: J7.pin15, MicroSD_Card_Pins.pin2
  N5: J6.pin1, MicroSD_Card_Pins.pin4
  N6: J6.pin2, MicroSD_Card_Pins.pin3
  N7: J6.pin3, MicroSD_Card_Pins.pin1
  N8: J6.pin5, Relay.pin3
  N9: J6.pin6, Relay.pin2
  N10: J6.pin8, RTClock_Pins.pin3
  N11: J6.pin9, RTClock_Pins.pin4
  N12: J6.pin10, Temperature_Sensors.pin2
  N13: J6.pin11, Temperature_Sensors.pin3
